// Logisim project garg_utkarsh.circ as structural Verilog: 7 circuits, main circuit main
module main (
  input  Clear,
  input  EN
);

  wire CLK, comparator_1_eq, comparator_2_eq, comparator_2_lt, comparator_3_eq, comparator_4_eq,
       comparator_5_eq, WrEN;
  wire [1:0] bit_extender_3_out, PC_Select;
  wire [3:0] ex_mem_buffer_1_opcode_out, ex_mem_buffer_1_rx_out, ex_mem_buffer_1_ry_out,
       idrr_ex_buffer_1_opcode_out, idrr_ex_buffer_1_rx_out, idrr_ex_buffer_1_ry_out,
       mem_wb_buffer_1_opcode_out, multiplexer_2_out, RegNo;
  wire [19:0] ex_mem_buffer_1_offset_out, idrr_ex_buffer_1_offset_out, if_idrr_buffer_1_inst_out_2;
  wire [23:0] bit_extender_1_out, bit_extender_4_out;
  wire [31:0] adder_1_out, adder_2_out, alu_1_out, bit_extender_2_out, dual_ported_register_file_1_out1,
       dual_ported_register_file_1_out2, ex_mem_buffer_1_rd_1_out, ex_mem_buffer_1_rd_2_out,
       ex_mem_buffer_1_result_out, idrr_ex_buffer_1_pc_out, idrr_ex_buffer_1_rd_1_out,
       idrr_ex_buffer_1_rd_2_out, if_idrr_buffer_1_pc_out, INPUT, multiplexer_1_out, PC_q, ram_1_data,
       rom_1_data;
  wire [31:20] if_idrr_buffer_1_inst_out;

  Clock Clock (.out(CLK));
  Register #(.width(32)) PC (.D(multiplexer_1_out), .en(EN), .Q(PC_q), .clk(CLK), .clr(Clear));
  Multiplexer #(.select(2), .width(32)) multiplexer_1 (
    .in0(idrr_ex_buffer_1_rd_1_out), .in1(adder_2_out), .in2(PC_q), .in3(adder_1_out),
    .out(multiplexer_1_out), .sel(PC_Select), .en(EN));
  Bit_Extender #(.in_width(32), .out_width(24)) bit_extender_1 (.in(PC_q), .out(bit_extender_1_out));
  Adder #(.width(32)) adder_1 (.a(PC_q), .b(32'h1), .out(adder_1_out));  // open: cin, cout
  ROM #(.addrWidth(24), .dataWidth(32)) rom_1 (.addr(bit_extender_1_out), .data(rom_1_data), .sel(EN));
  IF_IDRR_Buffer if_idrr_buffer_1 (
    .CLOCK(CLK), .EN(EN), .Clear(Clear), .PC_IN(adder_1_out), .Inst_IN(rom_1_data),
    .PC_OUT(if_idrr_buffer_1_pc_out), .Inst_OUT({if_idrr_buffer_1_inst_out, if_idrr_buffer_1_inst_out_2}));
  Multiplexer #(.width(4), .enable("false")) multiplexer_2 (
    .in0(if_idrr_buffer_1_inst_out_2[3:0]), .in1(if_idrr_buffer_1_inst_out[27:24]), .out(multiplexer_2_out),
    .sel(comparator_1_eq));
  Comparator #(.width(4)) comparator_1 (
    .a(4'b0011), .b(if_idrr_buffer_1_inst_out[31:28]), .eq(comparator_1_eq));  // open: gt, lt
  Comparator #(.width(4)) comparator_2 (
    .a(4'b0101), .b(if_idrr_buffer_1_inst_out[31:28]), .eq(comparator_2_eq), .lt(comparator_2_lt));  // open: gt
  Comparator #(.width(4)) comparator_3 (
    .a(4'b0110), .b(if_idrr_buffer_1_inst_out[31:28]), .eq(comparator_3_eq));  // open: gt, lt
  Dual_Ported_Register_File dual_ported_register_file_1 (
    .CLK(CLK), .WrREGNO(RegNo), .RdREGNO1(if_idrr_buffer_1_inst_out[23:20]), .RdREGNO2(multiplexer_2_out),
    .INPUT(INPUT), .OUT1(dual_ported_register_file_1_out1), .OUT2(dual_ported_register_file_1_out2),
    .WrEN(WrEN));
  IDRR_EX_Buffer idrr_ex_buffer_1 (
    .CLOCK(CLK), .EN(EN), .Clear(Clear), .PC_IN(if_idrr_buffer_1_pc_out),
    .Offset_IN(if_idrr_buffer_1_inst_out_2), .Rd_1_IN(dual_ported_register_file_1_out1),
    .Rd_2_IN(dual_ported_register_file_1_out2), .Opcode_IN(if_idrr_buffer_1_inst_out[31:28]),
    .Rx_IN(if_idrr_buffer_1_inst_out[27:24]), .Ry_IN(if_idrr_buffer_1_inst_out[23:20]),
    .PC_OUT(idrr_ex_buffer_1_pc_out), .Offset_OUT(idrr_ex_buffer_1_offset_out),
    .Rd_1_OUT(idrr_ex_buffer_1_rd_1_out), .Rd_2_OUT(idrr_ex_buffer_1_rd_2_out),
    .Opcode_OUT(idrr_ex_buffer_1_opcode_out), .Rx_OUT(idrr_ex_buffer_1_rx_out),
    .Ry_OUT(idrr_ex_buffer_1_ry_out));
  or or_1 (PC_Select[0], comparator_2_eq, comparator_2_lt);
  or or_2 (PC_Select[1], comparator_2_lt, comparator_3_eq);
  assign bit_extender_2_out = {{12{1'b0}}, if_idrr_buffer_1_inst_out_2};  // Bit_Extender bit_extender_2
  Adder #(.width(32)) adder_2 (
    .a(bit_extender_2_out), .b(idrr_ex_buffer_1_pc_out), .out(adder_2_out));  // open: cin, cout
  Bit_Extender #(.in_width(4), .out_width(2)) bit_extender_3 (
    .in(idrr_ex_buffer_1_opcode_out), .out(bit_extender_3_out));
  ALU alu_1 (.FUNC(bit_extender_3_out), .A(idrr_ex_buffer_1_rd_1_out), .B(idrr_ex_buffer_1_rd_2_out), .OUT(alu_1_out));
  EX_MEM_Buffer ex_mem_buffer_1 (
    .CLOCK(CLK), .EN(EN), .Clear(Clear), .Offset_IN(idrr_ex_buffer_1_offset_out),
    .Rd_1_IN(idrr_ex_buffer_1_rd_1_out), .Rd_2_IN(idrr_ex_buffer_1_rd_2_out),
    .Opcode_IN(idrr_ex_buffer_1_opcode_out), .Rx_IN(idrr_ex_buffer_1_rx_out),
    .Ry_IN(idrr_ex_buffer_1_ry_out), .Result_IN(alu_1_out), .Offset_OUT(ex_mem_buffer_1_offset_out),
    .Rd_1_OUT(ex_mem_buffer_1_rd_1_out), .Rd_2_OUT(ex_mem_buffer_1_rd_2_out),
    .Opcode_OUT(ex_mem_buffer_1_opcode_out), .Rx_OUT(ex_mem_buffer_1_rx_out),
    .Ry_OUT(ex_mem_buffer_1_ry_out), .Result_OUT(ex_mem_buffer_1_result_out));
  Bit_Extender #(.in_width(32), .out_width(24)) bit_extender_4 (
    .in(ex_mem_buffer_1_result_out), .out(bit_extender_4_out));
  Comparator #(.width(4)) comparator_4 (
    .a(4'b0100), .b(ex_mem_buffer_1_opcode_out), .eq(comparator_4_eq));  // open: gt, lt
  Comparator #(.width(4)) comparator_5 (
    .a(4'b0011), .b(ex_mem_buffer_1_opcode_out), .eq(comparator_5_eq));  // open: gt, lt
  RAM #(.addrWidth(24), .dataWidth(32), .bus("separate")) ram_1 (
    .addr(bit_extender_4_out), .din(ex_mem_buffer_1_rd_2_out), .data(ram_1_data), .str(comparator_4_eq),
    .clk(CLK), .ld(comparator_5_eq), .clr(Clear));  // open: sel
  MEM_WB_Buffer mem_wb_buffer_1 (
    .CLOCK(CLK), .EN(EN), .Clear(Clear), .Offset_IN(ex_mem_buffer_1_offset_out),
    .Rd_1_IN(ex_mem_buffer_1_rd_1_out), .Rd_2_IN(ex_mem_buffer_1_rd_2_out),
    .Opcode_IN(ex_mem_buffer_1_opcode_out), .Rx_IN(ex_mem_buffer_1_rx_out), .Ry_IN(ex_mem_buffer_1_ry_out),
    .Result_IN(ex_mem_buffer_1_result_out), .RAM_OUT_IN(ram_1_data), .Opcode_OUT(mem_wb_buffer_1_opcode_out),
    .Rx_OUT(RegNo), .RAM_OUT(INPUT));  // open: Offset_OUT, Rd_1_OUT, Rd_2_OUT, Ry_OUT, Result_OUT
  Comparator #(.width(4)) comparator_6 (.a(mem_wb_buffer_1_opcode_out), .b(4'b0100), .lt(WrEN));  // open: gt, eq

  // Other names for the same wires on the sheet: CLR = Clear
endmodule

module Dual_Ported_Register_File (
  input  CLK,
  input  WrEN,
  input  [3:0] WrREGNO,
  input  [3:0] RdREGNO1,
  input  [3:0] RdREGNO2,
  input  [31:0] INPUT,
  output [31:0] OUT1,
  output [31:0] OUT2
);

  wire En_a0, En_a1, En_a2, En_a3, En_a4, En_at, En_fp, En_k0, En_ra, En_s0, En_s1, En_s2, En_s3, En_sp,
       En_v0;
  wire [31:0] a0, a1, a2, a3, a4, at, fp, k0, ra, s0, s1, s2, s3, sp, v0, zero;

  Decoder #(.select(4), .disabled(0)) decoder_1 (
    .out1(En_at), .out2(En_v0), .out3(En_a0), .out4(En_a1), .out5(En_a2), .out6(En_a3), .out7(En_a4),
    .out8(En_s0), .out9(En_s1), .out10(En_s2), .out11(En_s3), .out12(En_k0), .out13(En_sp), .out14(En_fp),
    .out15(En_ra), .sel(WrREGNO));  // open: out0, en
  Register #(.width(32)) u_zero (.D(INPUT), .en(1'b0), .Q(zero), .clk(CLK));  // open: clr
  Register #(.width(32)) u_at (.D(INPUT), .en(En_at), .Q(at), .clk(CLK));  // open: clr
  Register #(.width(32)) u_v0 (.D(INPUT), .en(En_v0), .Q(v0), .clk(CLK));  // open: clr
  Register #(.width(32)) u_a0 (.D(INPUT), .en(En_a0), .Q(a0), .clk(CLK));  // open: clr
  Register #(.width(32)) u_a1 (.D(INPUT), .en(En_a1), .Q(a1), .clk(CLK));  // open: clr
  Register #(.width(32)) u_a2 (.D(INPUT), .en(En_a2), .Q(a2), .clk(CLK));  // open: clr
  Register #(.width(32)) u_a3 (.D(INPUT), .en(En_a3), .Q(a3), .clk(CLK));  // open: clr
  Register #(.width(32)) u_a4 (.en(En_a4), .Q(a4), .clk(CLK));  // open: D, clr
  Multiplexer #(.select(4), .width(32), .disabled(0), .enable("false")) multiplexer_1 (
    .in0(zero), .in1(at), .in2(v0), .in3(a0), .in4(a1), .in5(a2), .in6(a3), .in7(a4), .in8(s0), .in9(s1),
    .in10(s2), .in11(s3), .in12(k0), .in13(sp), .in14(fp), .in15(ra), .out(OUT2), .sel(RdREGNO2));
  Register #(.width(32)) u_s0 (.D(INPUT), .en(En_s0), .Q(s0), .clk(CLK));  // open: clr
  Register #(.width(32)) u_s1 (.D(INPUT), .en(En_s1), .Q(s1), .clk(CLK));  // open: clr
  Register #(.width(32)) u_s2 (.D(INPUT), .en(En_s2), .Q(s2), .clk(CLK));  // open: clr
  Register #(.width(32)) u_s3 (.en(En_s3), .Q(s3), .clk(CLK));  // open: D, clr
  Register #(.width(32)) u_k0 (.D(INPUT), .en(En_k0), .Q(k0), .clk(CLK));  // open: clr
  Register #(.width(32)) u_sp (.D(INPUT), .en(En_sp), .Q(sp), .clk(CLK));  // open: clr
  Register #(.width(32)) u_fp (.D(INPUT), .en(En_fp), .Q(fp), .clk(CLK));  // open: clr
  Register #(.width(32)) u_ra (.en(En_ra), .Q(ra), .clk(CLK));  // open: D, clr
  Multiplexer #(.select(4), .width(32), .disabled(0), .enable("false")) multiplexer_2 (
    .in0(zero), .in1(at), .in2(v0), .in3(a0), .in4(a1), .in5(a2), .in6(a3), .in7(a4), .in8(s0), .in9(s1),
    .in10(s2), .in11(s3), .in12(k0), .in13(sp), .in14(fp), .in15(ra), .out(OUT1), .sel(RdREGNO1));
endmodule

// IF/IDRR Buff
module IF_IDRR_Buffer (
  input  CLOCK,
  input  EN,
  input  Clear,
  input  [31:0] PC_IN,
  input  [31:0] Inst_IN,
  output [31:0] PC_OUT,
  output [31:0] Inst_OUT
);

  Register #(.width(32)) register_1 (.D(PC_IN), .en(EN), .Q(PC_OUT), .clk(CLOCK), .clr(Clear));
  Register #(.width(32)) register_2 (.D(Inst_IN), .en(EN), .Q(Inst_OUT), .clk(CLOCK), .clr(Clear));

  // Other names for the same wires on the sheet: CLK = CLOCK; CLR = Clear
endmodule

// IDRR/EX Buff
module IDRR_EX_Buffer (
  input  CLOCK,
  input  EN,
  input  Clear,
  input  [31:0] PC_IN,
  input  [19:0] Offset_IN,
  input  [31:0] Rd_1_IN,
  input  [31:0] Rd_2_IN,
  input  [3:0] Opcode_IN,
  input  [3:0] Rx_IN,
  input  [3:0] Ry_IN,
  output [31:0] PC_OUT,
  output [19:0] Offset_OUT,
  output [31:0] Rd_1_OUT,
  output [31:0] Rd_2_OUT,
  output [3:0] Opcode_OUT,
  output [3:0] Rx_OUT,
  output [3:0] Ry_OUT
);

  Register #(.width(32)) register_1 (.D(PC_IN), .en(EN), .Q(PC_OUT), .clk(CLOCK), .clr(Clear));
  Register #(.width(20)) register_2 (.D(Offset_IN), .en(EN), .Q(Offset_OUT), .clk(CLOCK), .clr(Clear));
  Register #(.width(32)) register_3 (.D(Rd_1_IN), .en(EN), .Q(Rd_1_OUT), .clk(CLOCK), .clr(Clear));
  Register #(.width(32)) register_4 (.D(Rd_2_IN), .en(EN), .Q(Rd_2_OUT), .clk(CLOCK), .clr(Clear));
  Register #(.width(4)) register_5 (.D(Opcode_IN), .en(EN), .Q(Opcode_OUT), .clk(CLOCK), .clr(Clear));
  Register #(.width(4)) register_6 (.D(Rx_IN), .en(EN), .Q(Rx_OUT), .clk(CLOCK), .clr(Clear));
  Register #(.width(4)) register_7 (.D(Ry_IN), .en(EN), .Q(Ry_OUT), .clk(CLOCK), .clr(Clear));

  // Other names for the same wires on the sheet: CLK = CLOCK; CLR = Clear
endmodule

module EX_MEM_Buffer (
  input  CLOCK,
  input  EN,
  input  Clear,
  input  [19:0] Offset_IN,
  input  [31:0] Rd_1_IN,
  input  [31:0] Rd_2_IN,
  input  [3:0] Opcode_IN,
  input  [3:0] Rx_IN,
  input  [3:0] Ry_IN,
  input  [31:0] Result_IN,
  output [19:0] Offset_OUT,
  output [31:0] Rd_1_OUT,
  output [31:0] Rd_2_OUT,
  output [3:0] Opcode_OUT,
  output [3:0] Rx_OUT,
  output [3:0] Ry_OUT,
  output [31:0] Result_OUT
);

  Register #(.width(20)) register_1 (.D(Offset_IN), .en(EN), .Q(Offset_OUT), .clk(CLOCK), .clr(Clear));
  Register #(.width(32)) register_2 (.D(Rd_1_IN), .en(EN), .Q(Rd_1_OUT), .clk(CLOCK), .clr(Clear));
  Register #(.width(32)) register_3 (.D(Rd_2_IN), .en(EN), .Q(Rd_2_OUT), .clk(CLOCK), .clr(Clear));
  Register #(.width(4)) register_4 (.D(Opcode_IN), .en(EN), .Q(Opcode_OUT), .clk(CLOCK), .clr(Clear));
  Register #(.width(4)) register_5 (.D(Rx_IN), .en(EN), .Q(Rx_OUT), .clk(CLOCK), .clr(Clear));
  Register #(.width(4)) register_6 (.D(Ry_IN), .en(EN), .Q(Ry_OUT), .clk(CLOCK), .clr(Clear));
  Register #(.width(32)) register_7 (.D(Result_IN), .en(EN), .Q(Result_OUT), .clk(CLOCK), .clr(Clear));

  // Other names for the same wires on the sheet: CLK = CLOCK; CLR = Clear
endmodule

module MEM_WB_Buffer (
  input  CLOCK,
  input  EN,
  input  Clear,
  input  [19:0] Offset_IN,
  input  [31:0] Rd_1_IN,
  input  [31:0] Rd_2_IN,
  input  [3:0] Opcode_IN,
  input  [3:0] Rx_IN,
  input  [3:0] Ry_IN,
  input  [31:0] Result_IN,
  input  [31:0] RAM_OUT_IN,
  output [19:0] Offset_OUT,
  output [31:0] Rd_1_OUT,
  output [31:0] Rd_2_OUT,
  output [3:0] Opcode_OUT,
  output [3:0] Rx_OUT,
  output [3:0] Ry_OUT,
  output [31:0] Result_OUT,
  output [31:0] RAM_OUT
);

  Register #(.width(20)) register_1 (.D(Offset_IN), .en(EN), .Q(Offset_OUT), .clk(CLOCK), .clr(Clear));
  Register #(.width(32)) register_2 (.D(Rd_1_IN), .en(EN), .Q(Rd_1_OUT), .clk(CLOCK), .clr(Clear));
  Register #(.width(32)) register_3 (.D(Rd_2_IN), .en(EN), .Q(Rd_2_OUT), .clk(CLOCK), .clr(Clear));
  Register #(.width(4)) register_4 (.D(Opcode_IN), .en(EN), .Q(Opcode_OUT), .clk(CLOCK), .clr(Clear));
  Register #(.width(4)) register_5 (.D(Rx_IN), .en(EN), .Q(Rx_OUT), .clk(CLOCK), .clr(Clear));
  Register #(.width(4)) register_6 (.D(Ry_IN), .en(EN), .Q(Ry_OUT), .clk(CLOCK), .clr(Clear));
  Register #(.width(32)) register_7 (.D(Result_IN), .en(EN), .Q(Result_OUT), .clk(CLOCK), .clr(Clear));
  Register #(.width(32)) register_8 (.D(RAM_OUT_IN), .en(EN), .Q(RAM_OUT), .clk(CLOCK), .clr(Clear));

  // Other names for the same wires on the sheet: CLK = CLOCK; CLR = Clear
endmodule

module ALU (
  input  [1:0] FUNC,
  input  [31:0] A,
  input  [31:0] B,
  output [31:0] OUT
);

  wire [31:0] adder_1_out, adder_2_out, nand_1_out, subtractor_1_out;

  Adder #(.width(32)) adder_1 (.a(A), .b(B), .out(adder_1_out), .cin(1'b0));  // open: cout
  assign nand_1_out = ~(A & B);  // NAND_Gate nand_1, 32 bits wide
  Subtractor #(.width(32)) subtractor_1 (.a(A), .b(B), .out(subtractor_1_out), .bin(1'b0));  // open: bout
  Adder #(.width(32)) adder_2 (.a(A), .b(B), .out(adder_2_out), .cin(1'b1));  // open: cout
  Multiplexer #(.select(2), .width(32), .disabled(0), .enable("false")) multiplexer_1 (
    .in0(adder_1_out), .in1(nand_1_out), .in2(subtractor_1_out), .in3(adder_2_out), .out(OUT), .sel(FUNC));
endmodule
